# Fritzing sketch Untitled Sketch 3 (saved by Fritzing 0.9.9b)
breadboards: 2

parts:
  Argon1 = Particle Argon
  BAT1 = Battery Holders [package=lipo-1100mAh]  # not connected
  OLED_I2C1 = OLED 128x64 I2C Monochrome Display
  Neopixel1 = Adafruit RBG Smart Neopixel [package="DIP (Dual Inline) [THT]"]
  Part1 = InvenSense MPU6050

nets:
  3.3V: Argon1.3.3V, OLED_I2C1.VDD, Neopixel1.+, Part1.VCC
  GND: Argon1.GND, OLED_I2C1.GND, Neopixel1.G, Part1.GND
  N1: Argon1.SDA, OLED_I2C1.SDA, Part1.SDA
  N2: Argon1.SCL, OLED_I2C1.SCK
  N3: Argon1.D8, Neopixel1.In

custom parts:
  Particle Argon: The Argon is a powerful Wi-Fi enabled development board that can act as either a standalone Wi-Fi endpoint or Wi-Fi enabled gateway for Particle Mesh networks. It is based on the Nordic nRF52840 and has built-in battery charging circuitry so it’s easy to connect a Li-Po and deploy your local network in minutes. The Argon is great for connecting existing projects to the Particle Device Cloud or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
